# Fritzing sketch Sketch (saved by Fritzing 0.9.3b)
breadboards: 1

parts:
  Part1 = Adafruit HUZZAH ESP8266 [part_number="Adafruit #2471"]
  NEOPIXEL1 = Neopixel Strip -- Black (30/m) [part_number=1376]
  VCC1 = 4 x AAA Battery Mount
  Part2 = Adafruit LSM9DS1 9DoF Breakout [part_number="Adafruit #3387"]

nets:
  N1: Part1.GPIO14, NEOPIXEL1.Din
  3.3V: Part1.3.3V, Part2.VIN
  N2: Part1.GPIO4, Part2.SDA
  N3: Part1.GPIO5, Part2.SCL
  GND: NEOPIXEL1.GND, VCC1.-, Part2.GND
  N4: NEOPIXEL1.+5V, VCC1.+

notes:
  3x AA (4.5V)

custom parts:
  Adafruit HUZZAH ESP8266: Add Internet to your next project with an adorable, bite-sized WiFi microcontroller, at a price you like! The ESP8266 processor from Espressif is an 80 MHz microcontroller with a full WiFi front-end (both as client and access point) and TCP/IP stack with DNS support as well. While this chip has been very popular, its also been very difficult to use. Most of the low cost modules are not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
  Neopixel Strip -- Black (30/m): These NeoPixel strips have 30 digitally-addressable pixel LEDs per meter and are very affordable and are only 12.5 mm wide, 10 mm if you remove the strip from the casing.
  Adafruit LSM9DS1 9DoF Breakout: Add motion, direction and orientation sensing to your Arduino project with this all-in-one 9-DOF sensor. Inside the chip are three sensors, one is a classic 3-axis accelerometer, which can tell you which direction is down towards the Earth (by measuring gravity) or how fast the board is accelerating in 3D space. The other is a 3-axis magnetometer that can sense where the strongest magnetic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
